# Fritzing sketch pcb-had (saved by Fritzing 0.9.2b)
circuit board: 4.95cm x 4.95cm
breadboards: 1

parts:
  vin = Pad [width=2.54 height=1.27 connect=center]
  gnd = Pad [width=2.54 height=1.27 connect=center]
  rst = Pad [width=2.54 height=1.27 connect=center]  # not connected
  vcc = Pad [width=2.54 height=1.27 connect=center]
  17 = Pad [width=2.54 height=1.27 connect=center]
  16 = Pad [width=2.54 height=1.27 connect=center]
  15 = Pad [width=2.54 height=1.27 connect=center]
  14 = Pad [width=2.54 height=1.27 connect=center]
  *13 = Pad [width=2.54 height=1.27 connect=center]
  12 = Pad [width=2.54 height=1.27 connect=center]
  11 = Pad [width=2.54 height=1.27 connect=center]
  10 = Pad [width=2.54 height=1.27 connect=center]
  tx0 = Pad [width=2.54 height=1.27 connect=center]
  rx1 = Pad [width=2.54 height=1.27 connect=center]
  rst_2 = Pad [width=2.54 height=1.27 connect=center]  # not connected
  gnd_2 = Pad [width=2.54 height=1.27 connect=center]
  2 = Pad [width=2.54 height=1.27 connect=center]
  3 = Pad [width=2.54 height=1.27 connect=center]
  4 = Pad [width=2.54 height=1.27 connect=center]
  5 = Pad [width=2.54 height=1.27 connect=center]
  6 = Pad [width=2.54 height=1.27 connect=center]
  7 = Pad [width=2.54 height=1.27 connect=center]
  8 = Pad [width=2.54 height=1.27 connect=center]
  9 = Pad [width=2.54 height=1.27 connect=center]
  scl = Pad [width=2.54 height=1.27 connect=center]
  sda = Pad [width=2.54 height=1.27 connect=center]
  A7 = Pad [width=2.54 height=1.27 connect=center]
  A6 = Pad [width=2.54 height=1.27 connect=center]
  U1 = mystery part, 3 pins [chip_label=?]
  U2 = mystery part, 3 pins [chip_label=?]
  U3 = mystery part, 3 pins [chip_label=?]
  U4 = mystery part, 3 pins [chip_label=?]
  U5 = mystery part, 3 pins [chip_label=?]
  U6 = mystery part, 3 pins [chip_label=?]
  U7 = mystery part, 3 pins [chip_label=?]
  U8 = mystery part, 3 pins [chip_label=?]
  U9 = mystery part, 3 pins [chip_label=?]
  U10 = mystery part, 3 pins [chip_label=?]
  U11 = mystery part, 3 pins [chip_label=?]
  U12 = mystery part, 3 pins [chip_label=?]
  +bat- = mystery part, 2 pins [chip_label=?]
  R1 = Resistor [tolerance=±5% resistance=220 package="0805 [SMD]"]
  R2 = Resistor [tolerance=±5% resistance=220 package="0805 [SMD]"]
  U13 = mystery part, 3 pins [chip_label=?]
  U14 = mystery part, 3 pins [chip_label=?]
  U15 = mystery part, 3 pins [chip_label=?]
  U16 = mystery part, 3 pins [chip_label=?]
  U17 = mystery part, 3 pins [chip_label=?]
  U18 = mystery part, 3 pins [chip_label=?]
  U19 = mystery part, 3 pins [chip_label=?]
  U20 = mystery part, 3 pins [chip_label=?]
  Pad1 = Pad [width=2.54 height=5.08 connect=center]
  on = Pad [width=2.54 height=5.08 connect=center]
  off = Pad [width=2.54 height=5.08 connect=center]  # not connected
  esp-01 = mystery part, 8 pins [chip_label=?]
  R3 = Resistor [tolerance=±5% resistance=220 package="0805 [SMD]"]
  rx_tx_gnd = mystery part, 3 pins [chip_label=?]
  scl_sda_gnd = mystery part, 3 pins [chip_label=?]
  C1 = Electrolytic Capacitor [capacitance=1µF package="100 mil [THT, electrolytic]"]
  R4 = Resistor [tolerance=±5% resistance=220 package="0805 [SMD]"]
  R5 = Resistor [tolerance=±5% resistance=220 package="0805 [SMD]"]
  J1 = double row female pin header, 6 pins [form="♀ (female)"]

nets:
  N1: vin.pad, U1.pin2, U2.pin2, U3.pin2, U4.pin2, U5.pin2, U6.pin2, Pad1.pad, esp-01.pin5, C1.+, R5.Pin_0
  N2: gnd.pad, U1.pin1, U2.pin1, U3.pin1, U4.pin1, U5.pin1, U6.pin1, U13.pin1, U14.pin1, U15.pin1, U16.pin1, U17.pin1, U18.pin1, U19.pin1, U20.pin1, scl_sda_gnd.pin1, C1.-
  N3: vcc.pad, R1.Pin_1, R2.Pin_1, U13.pin2, U14.pin2, U15.pin2, U16.pin2, U17.pin2, U18.pin2, U19.pin2, U20.pin2, R3.Pin_1
  N4: 17.pad, U19.pin3
  N5: 16.pad, U6.pin3
  N6: 15.pad, U5.pin3
  N7: 14.pad, U4.pin3
  N8: *13.pad, U17.pin3
  N9: 12.pad, U3.pin3
  N10: 11.pad, U2.pin3
  N11: 10.pad, U1.pin3
  N12: tx0.pad, U15.pin3
  N13: rx1.pad, U13.pin3
  N14: gnd_2.pad, U7.pin1, U8.pin1, U9.pin1, U10.pin1, U11.pin1, U12.pin1, +bat-.pin1, esp-01.pin1, rx_tx_gnd.pin1, R4.Pin_0, J1.pin3
  N15: 2.pad, U14.pin3
  N16: 3.pad, U20.pin3
  N17: 4.pad, U11.pin3
  N18: 5.pad, U12.pin3
  N19: 6.pad, U10.pin3
  N20: 7.pad, U9.pin3
  N21: 8.pad, U8.pin3
  N22: 9.pad, U7.pin3
  N23: scl.pad, R1.Pin_0, esp-01.pin2, scl_sda_gnd.pin3, J1.pin4
  N24: sda.pad, R2.Pin_0, esp-01.pin3, scl_sda_gnd.pin2, J1.pin5
  N25: A7.pad, U16.pin3, R4.Pin_1, R5.Pin_1
  N26: A6.pad, U18.pin3
  N27: U7.pin2, U8.pin2, U9.pin2, U10.pin2, U11.pin2, U12.pin2, J1.pin1, J1.pin2
  N28: +bat-.pin2, on.pad
  N29: esp-01.pin4, rx_tx_gnd.pin3
  N30: esp-01.pin7, R3.Pin_0
  N31: esp-01.pin8, rx_tx_gnd.pin2

notes:
  03 02 01 00 A6 A7 13 A3
